# Fritzing sketch 3軸加速度 (saved by Fritzing 0.9.4)
breadboards: 1

parts:
  U1 = GP-2106 [package=gp-2106]
  パーツ1 = Arduino Uno (Rev3)

nets:
  N1: U1.1PPS, パーツ1.5V
  N2: U1.ONOFF, パーツ1.GND
  N3: U1.RX, パーツ1.A3
  N4: U1.TX, パーツ1.A4/SDA
  N5: U1.VCC, パーツ1.A5/SCL
