# Fritzing sketch 人感センサ (saved by Fritzing 0.9.4)
breadboards: 1

parts:
  パーツ1 = Arduino Uno (Rev3)
  LED1 = LED - 5mm [color="Red (633nm)" package="5 mm [THT]"]
  R1 = Resistor [tolerance=±5% resistance=220 package=THT]
  パーツ2 = HC-SR501 Body Sensor Module

nets:
  N1: パーツ1.D10_PWM/SS, R1.Pin_1
  5V: パーツ1.5V, パーツ2.VCC
  N2: パーツ1.GND, LED1.anode
  N3: LED1.cathode, R1.Pin_0

custom parts:
  HC-SR501 Body Sensor Module: Pyroelectric Infrared PIR Motion Sensor Detector Module
