# Fritzing sketch 圧力フルカラー (saved by Fritzing 0.9.4)
breadboards: 1

parts:
  パーツ1 = Arduino Uno (Rev3)
  LED1 = RGB LED (com. cathode, rgb) [package="5 mm [THT]"]
  R1 = Resistor [tolerance=±5% resistance=220 package=THT]
  R2 = Resistor [tolerance=±5% resistance=220 package=THT]
  R3 = Resistor [tolerance=±5% resistance=220 package=THT]
  J1 = Basic Force Sensing Resistor (FSR) [package=THT]  # not connected
  R4 = Resistor [tolerance=±5% resistance=220 package=THT]

nets:
  N1: パーツ1.A0, R4.Pin_0
  N2: パーツ1.D5_PWM, R3.Pin_0
  N3: パーツ1.D6_PWM, R2.Pin_0
  N4: パーツ1.D7, R1.Pin_0
  N5: LED1.red_anode, R3.Pin_1
  N6: LED1.green_anode, R2.Pin_1
  N7: LED1.blue_anode, R1.Pin_1
