# Fritzing sketch 温湿度センサ (saved by Fritzing 0.9.4)
breadboards: 1

parts:
  DHT1 = Humidity and Temperature Sensor DHT11
  パーツ1 = Arduino Uno (Rev3)
  R1 = Resistor [tolerance=±5% resistance=220 package=THT]

nets:
  N1: DHT1.Vcc, R1.Pin_0
  N2: DHT1.GND_2, パーツ1.GND
  N3: パーツ1.D8, R1.Pin_1

custom parts:
  Humidity and Temperature Sensor DHT11: Digital relative humidity & temperature sensor DHT11
