# Fritzing sketch 照度センサ (saved by Fritzing 0.9.4)
breadboards: 1

parts:
  パーツ1 = Arduino Uno (Rev3)
  R1 = Photocell (LDR) [package=THT]
  R2 = Resistor [tolerance=±5% resistance=220 package=THT]

nets:
  N1: パーツ1.A0, R1.pin_0, R2.Pin_1
  N2: パーツ1.5V, R1.pin_1
  N3: パーツ1.GND, R2.Pin_0
