# Fritzing sketch 超音波距離 (saved by Fritzing 0.9.4)
breadboards: 1

parts:
  パーツ1 = Arduino Uno (Rev3)
  HC-SR04_Sensor_1 = HC-SR04 Ultrasonic Distance Sensor

nets:
  N1: パーツ1.D10_PWM/SS, HC-SR04_Sensor_1.ECHO
  N2: パーツ1.D11_PWM/MOSI, HC-SR04_Sensor_1.TRIG
  5V: パーツ1.5V, HC-SR04_Sensor_1.VCC
  GND: パーツ1.GND, HC-SR04_Sensor_1.GND
